# Fritzing sketch circuito (saved by Fritzing 0.9.0b)
breadboards: 1

parts:
  U2 = NodeMCU V1.0
  K1 = Relay [part_number=FRS1B-S package=THT]
  R3 = Resistor [tolerance=±5% resistance=10k package=THT]
  Power_plug1 = Power plug
  L1 = Solenoid
  S1 = Pushbutton [package="[THT]"]
  Q1 = NPN-Transistor [package="TO92 [THT]"]
  R1 = Resistor [tolerance=±5% resistance=47 package=THT]
  R5 = Resistor [tolerance=±5% resistance=220 package=THT]
  R6 = Resistor [tolerance=±5% resistance=220 package=THT]
  R4 = Resistor [tolerance=±5% resistance=220 package=THT]
  LED1 = LED - 5mm [color="Blue (430nm)" package="5 mm [THT]"]
  LED2 = LED - 5mm [color="Green (555nm)" package="5 mm [THT]"]
  LED3 = LED - 5mm [color="Red (633nm)" package="5 mm [THT]"]
  R7 = Resistor [tolerance=±5% resistance=10k package=THT]

nets:
  N1: U2.D2, R3.Pin_0
  N2: U2.3V3, R7.Pin_1
  N3: U2.GND, Q1.E, LED1.cathode, LED2.cathode, LED3.cathode
  N4: U2.D5, R4.Pin_0
  N5: U2.D6, R5.Pin_0
  N6: U2.D7, R6.Pin_0
  N7: U2.D8, S1.Pin_1, S1.Pin_2
  N8: K1.A, K1.COIL1, R1.Pin_0
  N9: K1.C1, K1.C2, Power_plug1.VCC
  N10: K1.COIL2, K1.B, L1.pin2
  N11: R3.Pin_1, Q1.B
  N12: Power_plug1.GND, L1.pin1
  N13: S1.Pin_3, S1.Pin_4, R7.Pin_0
  N14: Q1.C, R1.Pin_1
  N15: R5.Pin_1, LED2.anode
  N16: R6.Pin_1, LED1.anode
  N17: R4.Pin_1, LED3.anode

custom parts:
  NodeMCU V1.0: ESP8266 based NodeMCU
